# Fritzing sketch DIY-lost-plane-alarm-finder-and-10-watts-LED-visual-aids-for-easy-orientation (saved by Fritzing 0.9.2b)
breadboards: 1

parts:
  Part1 = Arduino Nano (Rev3.0)
  R1 = Resistor [tolerance=±5% resistance=10k package=THT]
  Q1 = Basic FET N-Channel [part_number=IRF630N package="TO220 [THT]"]
  LED = LED - 5mm [color="Red (633nm)" package="5 mm [THT]"]
  J1 = Piezo Speaker
  MR1 = MR16 10W Led Driver [chip_label=MR16 part_number=MR16 package="DIP (Dual Inline) [THT]"]
  R2 = Resistor [tolerance=±5% resistance=10k package=THT]
  U1 = 3S LIPO 3600mAh [package=lipo-110]
  Q2 = Basic FET N-Channel [part_number=IRF630N package="TO220 [THT]"]
  Generic_2_4Ghz_RC_6ch_Receiver = Generic 2.4Ghz RC 6ch Receiver [package="RC Receiver"]

nets:
  N1: Part1.GND, R1.Pin_0, Q1.source, R2.Pin_0, U1.-, Q2.source, Generic_2_4Ghz_RC_6ch_Receiver.AUX1_-
  N2: Part1.D2, Generic_2_4Ghz_RC_6ch_Receiver.AUX1_S
  N3: Part1.D3, Generic_2_4Ghz_RC_6ch_Receiver.GEAR_S
  N4: Part1.D8, R2.Pin_1, Q2.gate
  N5: Part1.D9, R1.Pin_1, Q1.gate
  N6: Part1.VIN, J1.pin2, MR1.IN+, U1.+
  N7: Q1.drain, MR1.IN-
  N8: LED.cathode, MR1.OUT-
  N9: LED.anode, MR1.OUT+
  N10: J1.pin1, Q2.drain

custom parts:
  MR16 10W Led Driver: A 2 input pins 2 output pins 10W LED driver
  3S LIPO 3600mAh: 3S 3600mAh Lipo-battery
  Generic 2.4Ghz RC 6ch Receiver: A PCB for prototyping a Generic 2.4Ghz RC 6ch Receiver
